# Fritzing sketch luci (saved by Fritzing 0.9.3b)

parts:
  Part1 = Arduino Uno (Rev3)
  U1 = RELAY [package=relay-g5q]  # not connected
  U2 = RELAY [package=relay-g5q]  # not connected
  U3 = RELAY [package=relay-g5q]  # not connected
  U4 = RELAY [package=relay-g5q]  # not connected
  U5 = RELAY [package=relay-g5q]  # not connected
  U6 = RELAY [package=relay-g5q]
  S1 = Toggle Switch [package=THT]  # not connected
  U7 = MOC3031-M [package=dil06]  # not connected
  U8 = TLP621 [package=THT]  # not connected
  U10 = TLP621 [package=THT]
  R1 = Resistor [tolerance=±5% resistance=220 package=THT]
  Q2 = NPN-Transistor [package="TO92 [THT]"]
  D1 = Rectifier Diode [part_number=1N4001 package="300 mil [THT]"]
  D2 = Rectifier Diode [part_number=1N4001 package="300 mil [THT]"]
  R2 = Resistor [tolerance=±5% resistance=220 package=THT]

nets:
  N1: Part1.D12/MISO, D2.cathode
  N2: Part1.5V, R2.Pin_0
  N3: U6.COIL2, Q2.C, D1.anode
  N4: U6.COIL1, U10.Pin_1, U10.Pin_4, D1.cathode, R2.Pin_1
  N5: U10.Pin_2, D2.anode
  N6: U10.Pin_3, R1.Pin_0
  N7: R1.Pin_1, Q2.B
  GND: Q2.E
